# Fritzing sketch sismo_alerta (saved by Fritzing 0.8.7b)
circuit board: 10cm x 7.1cm
breadboards: 1

parts:
  Part1 = Arduino Pro Mini v13
  R1 = Resistor [tolerance=±5% resistance=10M package=THT]
  LED1 = LED - 5mm [color="Red (633nm)" package="5 mm [THT]"]
  LED2 = LED - 5mm [color="Green (555nm)" package="5 mm [THT]"]
  J1 = Piezo Speaker
  R2 = Resistor [tolerance=±5% resistance=10M package=THT]
  LED3 = LED - 5mm [color="Red (633nm)" package="5 mm [THT]"]
  LED4 = LED - 5mm [color="Green (555nm)" package="5 mm [THT]"]
  R3 = Resistor [tolerance=±5% resistance=33 package=THT]
  R4 = Resistor [tolerance=±5% resistance=330 package=THT]
  R5 = Resistor [tolerance=±5% resistance=33 package=THT]
  R6 = Resistor [tolerance=±5% resistance=330 package=THT]
  S6 = Toggle Switch [package=THT]
  PART4 = Power Cell - LiPo Charger/Booster [part_number=PRT-11231]
  S2 = Pushbutton [package="[THT]"]
  Part2 = Digital FM Radio Receiver
  CONN1 = USB connector [part_number="USB B" package=THT]

nets:
  N1: Part1.A4, Part2.SDIO
  N2: Part1.A5, Part2.SCLK
  5V: Part1.RAW, R2.Pin_1, PART4.5V, CONN1.5V
  GND: Part1.GND, R1.Pin_1, LED1.cathode, LED2.cathode, J1.pin1, LED3.cathode, LED4.cathode, S6.COM, PART4.GND#2, S2.Pin_3, S2.Pin_4, Part2.GND
  VCC: Part1.VCC, PART4.VCC, Part2.3.3V
  N3: Part1.A0, R1.Pin_0, R2.Pin_0
  N4: Part1.D12/MISO, J1.pin2
  N5: Part1.D10_PWM/SS, Part2.!RST
  N6: Part1.D9_PWM, R3.Pin_0
  N7: Part1.D8, R4.Pin_0
  N8: Part1.D7, R5.Pin_0
  N9: Part1.D6_PWM, R6.Pin_0
  N10: Part1.D5_PWM, S2.Pin_1, S2.Pin_2
  N11: LED1.anode, R4.Pin_1
  N12: LED2.anode, R3.Pin_1
  N13: LED3.anode, R6.Pin_1
  N14: LED4.anode, R5.Pin_1
  N15: S6.L2, PART4.EN
  N16: PART4.GND#4, CONN1.GND, CONN1.chassis5, CONN1.chassis6

notes:
  github.com/manuel-rabade/sismo_alerta

custom parts:
  Power Cell - LiPo Charger/Booster: The PowerCell board is a single cell LiPo boost converter (to 3.3V and 5V) and micro-USB charger in one. The board comes with a JST connector for a single cell LiPo battery, a micro-USB connector for the 5V charge input, and selectable 3.3V and 5V output pins (labeled 'out'). There are also two charge pins broken out (labeled 'charge'), so you can use another 5V power source to charge the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
  Digital FM Radio Receiver: Description: This is a breakout board for the Silicon Laboratories Si4703 FM tuner chip. Beyond being a simple FM radio, the Si4703 is also capable of detecting and processing both Radio Data Service (RDS) and Radio Broadcast Data Service (RBDS) information. The Si4703 even does a very good job of filtering and carrier detection. It also enables data such as the station ID and song name to be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
